// Logisim project logisim.circ as structural Verilog: 8 circuits, main circuit main
module main (
  input  start,
  input  areset,
  output ready
);

  wire automat_1_write, clk_out;
  wire [3:0] automat_1_ram_address, automat_1_rom_address;
  wire [15:0] automat_1_data_to_ram, ram_1_data, rom_1_data;

  automat automat_1 (
    .data_from_rom(rom_1_data), .data_from_ram(ram_1_data), .start(start),
    .rom_address(automat_1_rom_address), .ram_address(automat_1_ram_address),
    .data_to_ram(automat_1_data_to_ram), .ready(ready), .write(automat_1_write), .clk(clk_out),
    .areset(areset));
  Clock clk (.out(clk_out));
  ROM #(.addrWidth(4), .dataWidth(16)) rom_1 (.addr(automat_1_rom_address), .data(rom_1_data));  // open: sel
  RAM #(.addrWidth(4), .dataWidth(16), .bus("separate")) ram_1 (
    .addr(automat_1_ram_address), .din(automat_1_data_to_ram), .data(ram_1_data), .str(automat_1_write),
    .clk(clk_out));  // open: sel, ld, clr

  // Notes on the sheet:
  //   contents of rom_1 (hex, n*v repeats v):
  //   1 2 3 4 5 6 7 8 9 a b c d e f 10
endmodule

// sort
module automat (
  input  [15:0] data_from_rom,
  input  [15:0] data_from_ram,
  input  start,
  input  clk,
  input  areset,
  output [3:0] rom_address,
  output [3:0] ram_address,
  output [15:0] data_to_ram,
  output ready,
  output write
);

  wire controllogic_1_outer_dec, controllogic_1_outer_inc1, controllogic_1_outer_init,
       controllogic_1_outer_pos, controllogic_1_pos_inc, controllogic_1_pos_init, controllogic_1_ram_rom,
       controllogic_1_register_direct, controllogic_1_romctn_inc, controllogic_1_romctn_init,
       datapath_1_doshift, datapath_1_in_rom, datapath_1_incpos, datapath_1_romzero;

  datapath datapath_1 (
    .clk(clk), .areset(areset), .pos_init(controllogic_1_pos_init), .romCtn_init(controllogic_1_romctn_init),
    .pos_inc(controllogic_1_pos_inc), .romCtn_inc(controllogic_1_romctn_inc),
    .outer_init(controllogic_1_outer_init), .outer_dec(controllogic_1_outer_dec), .in_rom(datapath_1_in_rom),
    .doShift(datapath_1_doshift), .rom_address(rom_address), .ram_address(ram_address),
    .data_from_rom(data_from_rom), .data_to_ram(data_to_ram), .data_from_ram(data_from_ram),
    .ram_rom(controllogic_1_ram_rom), .outer_inc1(controllogic_1_outer_inc1),
    .outer_pos(controllogic_1_outer_pos), .register_direct(controllogic_1_register_direct),
    .romZero(datapath_1_romzero), .incPos(datapath_1_incpos));
  controllogic controllogic_1 (
    .doShift(datapath_1_doshift), .in_rom(datapath_1_in_rom), .incPos(datapath_1_incpos),
    .romZero(datapath_1_romzero), .start(start), .pos_init(controllogic_1_pos_init),
    .romCtn_init(controllogic_1_romctn_init), .pos_inc(controllogic_1_pos_inc),
    .romCtn_inc(controllogic_1_romctn_inc), .outer_init(controllogic_1_outer_init),
    .outer_inc1(controllogic_1_outer_inc1), .outer_dec(controllogic_1_outer_dec),
    .outer_pos(controllogic_1_outer_pos), .ram_rom(controllogic_1_ram_rom),
    .register_direct(controllogic_1_register_direct), .ready(ready), .write(write), .areset(areset), .clk(clk));
endmodule

module datapath (
  input  pos_init,
  input  romCtn_init,
  input  pos_inc,
  input  romCtn_inc,
  input  outer_init,
  input  outer_inc1,
  input  outer_dec,
  input  clk,
  input  areset,
  input  outer_pos,
  input  [15:0] data_from_ram,
  input  [15:0] data_from_rom,
  input  ram_rom,
  input  register_direct,
  output doShift,
  output [3:0] rom_address,
  output in_rom,
  output [3:0] ram_address,
  output [15:0] data_to_ram,
  output incPos,
  output romZero
);

  wire comparator_1_lt, comparator_2_eq, comparator_2_gt, comparator_3_eq, comparator_3_lt, comparator_6_lt,
       or_2_out;
  wire [4:0] adder_1_out, multiplexer_3_out, multiplexer_4_out, multiplexer_5_out, outer_out, Pos_out,
       romCtn_out, subtractor_1_out;
  wire [15:0] multiplexer_1_out, register_1_q;

  // Probe on data_from_rom
  upCounter Pos (
    .Increment(pos_inc), .Write_init(pos_init), .Out(Pos_out), .clk(clk), .areset(areset), .Init({5{1'b0}}));
  // Probe on data_from_ram
  // Probe on Pos_out
  Register #(.width(16)) register_1 (.D(data_from_ram), .Q(register_1_q), .clk(clk), .clr(areset));  // open: en
  Multiplexer #(.width(16)) multiplexer_1 (
    .in0(data_from_ram), .in1(data_from_rom), .out(multiplexer_1_out), .sel(ram_rom));  // open: en
  Comparator #(.width(5), .mode("unsigned")) comparator_1 (
    .a(Pos_out), .b(romCtn_out), .lt(comparator_1_lt));  // open: gt, eq
  Comparator #(.width(5)) comparator_2 (
    .a(outer_out), .b(Pos_out), .gt(comparator_2_gt), .eq(comparator_2_eq));  // open: lt
  upCounter romCtn (
    .Increment(romCtn_inc), .Write_init(romCtn_init), .Out(romCtn_out), .clk(clk), .areset(areset),
    .Init({5{1'b0}}));
  // Probe on romCtn_out
  Multiplexer #(.width(16)) multiplexer_2 (
    .in0(register_1_q), .in1(multiplexer_1_out), .out(data_to_ram), .sel(register_direct));  // open: en
  // Probe on data_to_ram
  or or_1 (doShift, comparator_2_gt, comparator_2_eq);
  Comparator #(.width(16), .mode("unsigned")) comparator_3 (
    .a(data_from_ram), .b(data_from_rom), .eq(comparator_3_eq), .lt(comparator_3_lt));  // open: gt
  Comparator #(.width(16), .mode("unsigned")) comparator_4 (
    .a(data_from_rom), .b({16{1'b0}}), .eq(romZero));  // open: gt, lt
  Bit_Extender #(.in_width(5), .out_width(4)) bit_extender_1 (.in(romCtn_out), .out(rom_address));
  Comparator #(.width(5), .mode("unsigned")) comparator_5 (.a(romCtn_out), .b(5'b10000), .lt(in_rom));  // open: gt, eq
  // Probe on subtractor_1_out
  downCounter outer (
    .Init(subtractor_1_out), .Decrement(outer_dec), .Write_init(outer_init), .Out(outer_out), .clk(clk),
    .areset(areset));
  Subtractor #(.width(5)) subtractor_1 (.a(romCtn_out), .b(5'b00001), .out(subtractor_1_out));  // open: bin, bout
  or or_2 (or_2_out, comparator_3_eq, comparator_3_lt);
  // Probe on rom_address
  // Probe on outer_out
  and and_1 (incPos, comparator_1_lt, or_2_out);
  Multiplexer #(.width(5)) multiplexer_3 (
    .in0(outer_out), .in1(adder_1_out), .out(multiplexer_3_out), .sel(outer_inc1));  // open: en
  Adder #(.width(5)) adder_1 (.a(outer_out), .b(5'b00001), .out(adder_1_out));  // open: cin, cout
  Multiplexer #(.width(5)) multiplexer_4 (
    .in0(multiplexer_3_out), .in1(Pos_out), .out(multiplexer_4_out), .sel(outer_pos));  // open: en
  Comparator #(.width(5)) comparator_6 (.a(multiplexer_4_out), .b({5{1'b0}}), .lt(comparator_6_lt));  // open: gt, eq
  Bit_Extender #(.in_width(5), .out_width(4), .\type ("input")) bit_extender_2 (
    .in(multiplexer_5_out), .out(ram_address));  // open: extend
  Multiplexer #(.width(5)) multiplexer_5 (
    .in0(multiplexer_4_out), .in1({5{1'b0}}), .out(multiplexer_5_out), .sel(comparator_6_lt));  // open: en
endmodule

module controllogic (
  input  in_rom,
  input  romZero,
  input  incPos,
  input  doShift,
  input  start,
  input  clk,
  input  areset,
  output pos_init,
  output pos_inc,
  output romCtn_init,
  output romCtn_inc,
  output outer_init,
  output outer_dec,
  output ram_rom,
  output register_direct,
  output outer_inc1,
  output outer_pos,
  output write,
  output ready
);

  wire d_ff_1_q, d_ff_2_q, d_ff_3_q, d_ff_4_q, nsl_1_ns0, nsl_1_ns1, nsl_1_ns2, nsl_1_ns3;

  nsl nsl_1 (
    .s3(d_ff_1_q), .s2(d_ff_2_q), .s1(d_ff_3_q), .s0(d_ff_4_q), .in_rom(in_rom), .romZero(romZero),
    .incPos(incPos), .doShift(doShift), .start(start), .ns3(nsl_1_ns3), .ns2(nsl_1_ns2), .ns1(nsl_1_ns1),
    .ns0(nsl_1_ns0));
  D_Flip_Flop d_ff_1 (.clk(clk), .D(nsl_1_ns3), .Q(d_ff_1_q), .reset(areset));  // open: Qn, preset, en
  D_Flip_Flop d_ff_2 (.clk(clk), .D(nsl_1_ns2), .Q(d_ff_2_q), .reset(areset));  // open: Qn, preset, en
  D_Flip_Flop d_ff_3 (.clk(clk), .D(nsl_1_ns1), .Q(d_ff_3_q), .reset(areset));  // open: Qn, preset, en
  D_Flip_Flop d_ff_4 (.clk(clk), .D(nsl_1_ns0), .Q(d_ff_4_q), .reset(areset));  // open: Qn, preset, en
  outputlogic outputlogic_1 (
    .s3(d_ff_1_q), .s2(d_ff_2_q), .s1(d_ff_3_q), .s0(d_ff_4_q), .pos_init(pos_init), .pos_inc(pos_inc),
    .romCtn_init(romCtn_init), .romCtn_inc(romCtn_inc), .outer_init(outer_init), .outer_dec(outer_dec),
    .ram_rom(ram_rom), .register_direct(register_direct), .outer_inc1(outer_inc1), .outer_pos(outer_pos),
    .write(write), .ready(ready));
endmodule

module upCounter (
  input  [4:0] Init,
  input  clk,
  input  areset,
  input  Increment,
  input  Write_init,
  output [4:0] Out
);

  wire [4:0] adder_1_out, multiplexer_1_out, multiplexer_2_out;

  Multiplexer #(.width(5)) multiplexer_1 (
    .in0(Out), .in1(Init), .out(multiplexer_1_out), .sel(Write_init));  // open: en
  Adder #(.width(5)) adder_1 (.a(multiplexer_1_out), .b(5'b00001), .out(adder_1_out));  // open: cin, cout
  Multiplexer #(.width(5)) multiplexer_2 (
    .in0(multiplexer_1_out), .in1(adder_1_out), .out(multiplexer_2_out), .sel(Increment));  // open: en
  Register #(.width(5)) register_1 (.D(multiplexer_2_out), .Q(Out), .clk(clk), .clr(areset));  // open: en
endmodule

module downCounter (
  input  [4:0] Init,
  input  clk,
  input  areset,
  input  Decrement,
  input  Write_init,
  output [4:0] Out
);

  wire [4:0] multiplexer_1_out, multiplexer_2_out, subtractor_1_out;

  Multiplexer #(.width(5)) multiplexer_1 (
    .in0(Out), .in1(Init), .out(multiplexer_1_out), .sel(Write_init));  // open: en
  Subtractor #(.width(5)) subtractor_1 (
    .a(multiplexer_1_out), .b(5'b00001), .out(subtractor_1_out));  // open: bin, bout
  Multiplexer #(.width(5)) multiplexer_2 (
    .in0(multiplexer_1_out), .in1(subtractor_1_out), .out(multiplexer_2_out), .sel(Decrement));  // open: en
  Register #(.width(5)) register_1 (.D(multiplexer_2_out), .Q(Out), .clk(clk), .clr(areset));  // open: en
endmodule

module nsl (
  input  s3,
  input  s2,
  input  s1,
  input  s0,
  input  in_rom,
  input  romZero,
  input  incPos,
  input  doShift,
  input  start,
  output ns3,
  output ns2,
  output ns1,
  output ns0
);

  wire and_1_out, and_2_out, and_3_out, and_4_out, and_5_out, and_6_out, and_7_out, and_8_out, and_9_out,
       and_10_out, and_11_out, and_12_out, and_13_out, and_14_out, and_15_out, and_16_out, and_17_out,
       and_18_out, and_19_out, and_20_out, and_21_out, and_22_out, and_23_out, and_24_out, and_25_out,
       and_26_out, and_27_out, and_28_out, and_29_out, and_30_out, not_1_out, not_2_out, not_3_out,
       not_4_out, not_5_out, not_6_out, not_7_out, not_8_out, not_9_out, not_10_out, not_11_out, not_12_out,
       not_13_out, not_14_out, not_15_out, not_16_out, not_17_out, not_18_out, not_19_out, not_20_out,
       not_21_out, not_22_out, not_23_out, not_24_out, not_25_out, not_26_out, not_27_out, not_28_out,
       not_29_out, not_30_out, not_31_out, not_32_out, not_33_out, not_34_out, not_35_out, not_36_out,
       not_37_out, not_38_out, not_39_out, not_40_out, not_41_out, not_42_out, not_43_out, not_44_out,
       not_45_out, not_46_out, not_47_out, not_48_out, not_49_out, not_50_out, not_51_out, not_52_out,
       not_53_out, not_54_out, not_55_out, not_56_out, not_57_out, not_58_out, not_59_out, not_60_out,
       not_61_out, not_62_out, not_63_out, not_64_out, not_65_out, not_66_out, not_67_out, not_68_out,
       not_69_out, not_70_out, not_71_out, not_72_out, not_73_out;

  not not_1 (not_1_out, s3);
  not not_2 (not_2_out, s2);
  not not_3 (not_3_out, s2);
  not not_4 (not_4_out, s1);
  not not_5 (not_5_out, s0);
  not not_6 (not_6_out, s2);
  not not_7 (not_7_out, s1);
  not not_8 (not_8_out, s2);
  not not_9 (not_9_out, s0);
  not not_10 (not_10_out, s2);
  not not_11 (not_11_out, s1);
  not not_12 (not_12_out, s0);
  not not_13 (not_13_out, doShift);
  not not_14 (not_14_out, s1);
  not not_15 (not_15_out, s0);
  not not_16 (not_16_out, s3);
  not not_17 (not_17_out, s2);
  not not_18 (not_18_out, romZero);
  not not_19 (not_19_out, s3);
  not not_20 (not_20_out, s1);
  not not_21 (not_21_out, s0);
  not not_22 (not_22_out, s3);
  not not_23 (not_23_out, s0);
  not not_24 (not_24_out, s3);
  not not_25 (not_25_out, s1);
  not not_26 (not_26_out, s3);
  not not_27 (not_27_out, s1);
  not not_28 (not_28_out, incPos);
  not not_29 (not_29_out, s2);
  not not_30 (not_30_out, s1);
  not not_31 (not_31_out, s0);
  not not_32 (not_32_out, doShift);
  not not_33 (not_33_out, s1);
  not not_34 (not_34_out, s0);
  not not_35 (not_35_out, s3);
  not not_36 (not_36_out, s2);
  not not_37 (not_37_out, s1);
  not not_38 (not_38_out, s3);
  not not_39 (not_39_out, s2);
  not not_40 (not_40_out, s0);
  not not_41 (not_41_out, s1);
  not not_42 (not_42_out, s3);
  not not_43 (not_43_out, s1);
  not not_44 (not_44_out, s3);
  not not_45 (not_45_out, s1);
  not not_46 (not_46_out, incPos);
  not not_47 (not_47_out, s2);
  not not_48 (not_48_out, s1);
  not not_49 (not_49_out, s2);
  not not_50 (not_50_out, s0);
  not not_51 (not_51_out, s3);
  not not_52 (not_52_out, s2);
  not not_53 (not_53_out, s1);
  not not_54 (not_54_out, s0);
  not not_55 (not_55_out, s3);
  not not_56 (not_56_out, s2);
  not not_57 (not_57_out, s0);
  not not_58 (not_58_out, s1);
  not not_59 (not_59_out, s3);
  not not_60 (not_60_out, s1);
  not not_61 (not_61_out, s0);
  not not_62 (not_62_out, s3);
  not not_63 (not_63_out, s0);
  not not_64 (not_64_out, s3);
  not not_65 (not_65_out, s1);
  not not_66 (not_66_out, incPos);
  not not_67 (not_67_out, s2);
  not not_68 (not_68_out, s1);
  not not_69 (not_69_out, s0);
  not not_70 (not_70_out, s2);
  not not_71 (not_71_out, s0);
  not not_72 (not_72_out, s1);
  not not_73 (not_73_out, s0);
  and and_1 (and_1_out, not_1_out, s2, s1, s0);
  and and_2 (and_2_out, s3, not_2_out, s1, s0);
  and and_3 (and_3_out, s3, not_3_out, not_4_out, not_5_out, doShift);
  and and_4 (and_4_out, s3, not_6_out, not_7_out, s0);
  and and_5 (and_5_out, s3, not_8_out, s1, not_9_out);
  and and_6 (and_6_out, s3, not_10_out, not_11_out, not_12_out, not_13_out);
  and and_7 (and_7_out, s3, s2, not_14_out, not_15_out);
  and and_8 (and_8_out, not_16_out, not_17_out, s1, s0, not_18_out);
  and and_9 (and_9_out, not_19_out, s2, not_20_out, not_21_out);
  and and_10 (and_10_out, not_22_out, s2, s1, not_23_out);
  and and_11 (and_11_out, not_24_out, s2, not_25_out, s0, incPos);
  and and_12 (and_12_out, not_26_out, s2, not_27_out, s0, not_28_out);
  and and_13 (and_13_out, s3, not_29_out, not_30_out, not_31_out, not_32_out);
  and and_14 (and_14_out, s3, s2, not_33_out, not_34_out);
  and and_15 (and_15_out, not_35_out, not_36_out, not_37_out, s0);
  and and_16 (and_16_out, not_38_out, not_39_out, s1, not_40_out, in_rom);
  and and_17 (and_17_out, s3, s2, not_41_out, s0);
  and and_18 (and_18_out, not_42_out, s2, not_43_out, s0, incPos);
  and and_19 (and_19_out, not_44_out, s2, not_45_out, s0, not_46_out);
  and and_20 (and_20_out, s3, not_47_out, not_48_out, s0);
  and and_21 (and_21_out, s3, not_49_out, s1, not_50_out);
  and and_22 (and_22_out, not_51_out, not_52_out, not_53_out, not_54_out, start);
  and and_23 (and_23_out, not_55_out, not_56_out, s1, not_57_out, in_rom);
  and and_24 (and_24_out, s3, s2, not_58_out, s0);
  and and_25 (and_25_out, not_59_out, s2, not_60_out, not_61_out);
  and and_26 (and_26_out, not_62_out, s2, s1, not_63_out);
  and and_27 (and_27_out, not_64_out, s2, not_65_out, s0, not_66_out);
  and and_28 (and_28_out, s3, not_67_out, not_68_out, not_69_out, doShift);
  and and_29 (and_29_out, s3, not_70_out, s1, not_71_out);
  and and_30 (and_30_out, s3, s2, not_72_out, not_73_out);
  or or_1 (ns3, and_1_out, and_2_out, and_3_out, and_4_out, and_5_out, and_6_out, and_7_out);
  or or_2 (ns2, and_8_out, and_9_out, and_10_out, and_11_out, and_12_out, and_13_out, and_14_out);
  or or_3 (ns1, and_15_out, and_16_out, and_17_out, and_18_out, and_19_out, and_20_out, and_21_out);
  or or_4 (ns0, and_22_out, and_23_out, and_24_out, and_25_out, and_26_out, and_27_out, and_28_out, and_29_out, and_30_out);
endmodule

module outputlogic (
  input  s3,
  input  s2,
  input  s1,
  input  s0,
  output pos_init,
  output pos_inc,
  output romCtn_init,
  output romCtn_inc,
  output outer_init,
  output outer_dec,
  output ram_rom,
  output register_direct,
  output outer_inc1,
  output outer_pos,
  output write,
  output ready
);

  wire and_8_out, and_9_out, and_11_out, and_12_out, and_13_out, and_14_out, not_1_out, not_2_out, not_3_out,
       not_4_out, not_5_out, not_6_out, not_7_out, not_8_out, not_9_out, not_10_out, not_11_out, not_12_out,
       not_13_out, not_14_out, not_15_out, not_16_out, not_17_out, not_18_out, not_19_out, not_20_out,
       not_21_out, not_22_out, not_23_out, not_24_out, not_25_out, not_26_out, not_27_out, not_28_out,
       not_29_out, not_30_out, not_31_out;

  not not_1 (not_1_out, s3);
  not not_2 (not_2_out, s1);
  not not_3 (not_3_out, s0);
  not not_4 (not_4_out, s3);
  not not_5 (not_5_out, s0);
  not not_6 (not_6_out, s3);
  not not_7 (not_7_out, s2);
  not not_8 (not_8_out, s1);
  not not_9 (not_9_out, s1);
  not not_10 (not_10_out, s3);
  not not_11 (not_11_out, s2);
  not not_12 (not_12_out, s1);
  not not_13 (not_13_out, s0);
  not not_14 (not_14_out, s2);
  not not_15 (not_15_out, s1);
  not not_16 (not_16_out, s1);
  not not_17 (not_17_out, s0);
  not not_18 (not_18_out, s2);
  not not_19 (not_19_out, s0);
  not not_20 (not_20_out, s1);
  not not_21 (not_21_out, s0);
  not not_22 (not_22_out, s3);
  not not_23 (not_23_out, s1);
  not not_24 (not_24_out, s1);
  not not_25 (not_25_out, s0);
  not not_26 (not_26_out, s2);
  not not_27 (not_27_out, s0);
  not not_28 (not_28_out, s3);
  not not_29 (not_29_out, s2);
  not not_30 (not_30_out, s1);
  not not_31 (not_31_out, s0);
  and and_1 (pos_init, not_1_out, s2, not_2_out, not_3_out);
  and and_2 (pos_inc, not_4_out, s2, s1, not_5_out);
  and and_3 (romCtn_init, not_6_out, not_7_out, not_8_out, s0);
  and and_4 (romCtn_inc, s3, s2, not_9_out, s0);
  and and_5 (outer_init, not_10_out, s2, s1, s0);
  and and_6 (outer_dec, s3, not_11_out, s1, s0);
  and and_7 (ram_rom, s3, s2, not_12_out, not_13_out);
  and and_8 (and_8_out, s3, not_14_out, not_15_out, s0);
  or or_1 (register_direct, and_8_out, and_9_out);
  and and_9 (and_9_out, s3, s2, not_16_out, not_17_out);
  and and_10 (outer_inc1, s3, not_18_out, s1, not_19_out);
  and and_11 (and_11_out, s3, s2, not_20_out, not_21_out);
  or or_2 (outer_pos, and_11_out, and_12_out);
  and and_12 (and_12_out, not_22_out, s2, not_23_out, s0);
  and and_13 (and_13_out, s3, s2, not_24_out, not_25_out);
  or or_3 (write, and_13_out, and_14_out);
  and and_14 (and_14_out, s3, not_26_out, s1, not_27_out);
  and and_15 (ready, not_28_out, not_29_out, not_30_out, not_31_out);
endmodule
